# Fritzing sketch ATtiny85-flash (saved by Fritzing 0.9.2b)
breadboards: 1

parts:
  Part1 = Arduino Uno (Rev3)
  U1 = attiny85 [package=dip]
  R1 = Resistor [tolerance=±5% resistance=220 package="2010 [SMD]"]
  LED1 = LED - 3mm [color="Red (633nm)" package="3 mm [THT]"]

nets:
  N1: Part1.D10_PWM/SS, U1.Pin_1
  N2: Part1.D11_PWM/MOSI, U1.Pin_5
  N3: Part1.D12/MISO, U1.Pin_6
  N4: Part1.D13/SCK, U1.Pin_7
  N5: Part1.5V, U1.Pin_8
  N6: Part1.GND, U1.Pin_4, LED1.cathode
  N7: U1.Pin_3, R1.Pin_0
  N8: R1.Pin_1, LED1.anode
