# Fritzing sketch bb_rangeSensor_module (saved by Fritzing 0.9.2b)
breadboards: 1

parts:
  Part1 = Spark Core (v1.0)
  C1 = Electrolytic Capacitor [capacitance=1000μF package="1010 [SMD, electrolytic]"]
  U1 = LIPO-2000mAh [package=lipo-2000]
  CHARGER1 = USB_LiIon_LiPoly_Charger_v1.2
  Part2 = HC-SR04 Ultrasonic Rangemeter
  R1 = Resistor [tolerance=±5% resistance=470 package="1206 [SMD]"]
  R2 = Resistor [tolerance=±5% resistance=470 package="1206 [SMD]"]

nets:
  GND: Part1.GND, C1.-, CHARGER1.load_minus_1, Part2.GND, R2.Pin_1
  VIN: Part1.VIN, C1.+, CHARGER1.load_plus_1, Part2.VCC
  N1: Part1.D4, Part2.Trig
  N2: Part1.D5, R1.Pin_1, R2.Pin_0
  N3: U1.+, CHARGER1.batt_plus_1
  N4: U1.-, CHARGER1.batt_minus_1
  N5: Part2.Echo, R1.Pin_0
