# Fritzing sketch bb_servo_module (saved by Fritzing 0.9.2b)
breadboards: 1

parts:
  Part1 = Spark Core (v1.0)
  C1 = Electrolytic Capacitor [capacitance=1000μF package="1010 [SMD, electrolytic]"]
  U1 = LIPO-2000mAh [package=lipo-2000]
  CHARGER1 = USB_LiIon_LiPoly_Charger_v1.2
  J1 = Basic Servo
  D1 = Diode [part_number=1N4001 package=diode-1n4148]

nets:
  N1: Part1.D1, J1.pulse
  N2: C1.-, CHARGER1.load_minus_1, J1.gnd, D1.A
  N3: C1.+, CHARGER1.load_plus_1, J1.vcc, D1.C
  N4: U1.+, CHARGER1.batt_plus_1
  N5: U1.-, CHARGER1.batt_minus_1
