# Fritzing sketch bb_battery_module (saved by Fritzing 0.9.2b)
breadboards: 1

parts:
  Part1 = Spark Core (v1.0)
  C1 = Electrolytic Capacitor [capacitance=1000μF package="1010 [SMD, electrolytic]"]
  U1 = LIPO-2000mAh [package=lipo-2000]
  CHARGER1 = USB_LiIon_LiPoly_Charger_v1.2

nets:
  N1: Part1.GND, C1.-, CHARGER1.load_minus_1
  N2: Part1.VIN, C1.+, CHARGER1.load_plus_1
  N3: U1.+, CHARGER1.batt_plus_1
  N4: U1.-, CHARGER1.batt_minus_1
