# Fritzing sketch bb_complete_circuit (saved by Fritzing 0.9.2b)
breadboards: 1

parts:
  Part1 = Spark Core (v1.0)
  C1 = Electrolytic Capacitor [capacitance=1000μF package="1010 [SMD, electrolytic]"]
  U1 = LIPO-2000mAh [package=lipo-2000]
  CHARGER1 = USB_LiIon_LiPoly_Charger_v1.2
  neopixel1 = Neopixel Ring 16  # not connected
  MIC1 = MAX4466 Electret Microphone Breakout Board  # not connected
  D1 = Diode [package=diode-1n4148]  # not connected
  Q1 = NPN-Transistor [package="TO92 [THT]"]
  R1 = Resistor [tolerance=±5% resistance=470 package="1206 [SMD]"]
  R2 = Resistor [tolerance=±5% resistance=470 package="1206 [SMD]"]
  R3 = Resistor [tolerance=±5% resistance=470 package="1206 [SMD]"]
  Part2 = HC-SR04 Ultrasonic Rangemeter
  J1 = Basic Servo  # not connected

nets:
  N1: Part1.GND, C1.-, CHARGER1.load_minus_1, R2.Pin_1
  N2: Part1.VIN, C1.+, CHARGER1.load_plus_1
  N3: U1.+, CHARGER1.batt_plus_1
  N4: U1.-, CHARGER1.batt_minus_1
  N5: Q1.B, R3.Pin_0
  N6: R1.Pin_0, Part2.Echo
  N7: R1.Pin_1, R2.Pin_0

custom parts:
  Neopixel Ring 16: Neopixel Ring x16
  MAX4466 Electret Microphone Breakout Board: MAX4466 Electrec Microphone Breakout Board
