# Fritzing sketch bb_neopixel_sound_module (saved by Fritzing 0.9.2b)
breadboards: 1

parts:
  Part1 = Spark Core (v1.0)
  C1 = Electrolytic Capacitor [capacitance=1000μF package="1010 [SMD, electrolytic]"]
  U1 = LIPO-2000mAh [package=lipo-2000]
  CHARGER1 = USB_LiIon_LiPoly_Charger_v1.2
  neopixel1 = Neopixel Ring 16
  MIC1 = MAX4466 Electret Microphone Breakout Board

nets:
  N1: Part1.A0, MIC1.out
  GND: Part1.GND, C1.-, CHARGER1.load_minus_1, neopixel1.GND, MIC1.GND
  VIN: Part1.VIN, C1.+, CHARGER1.load_plus_1, neopixel1.VCC
  N2: Part1.D2, neopixel1.IN
  N3: Part1.3V3*, MIC1.VCC
  N4: U1.+, CHARGER1.batt_plus_1
  N5: U1.-, CHARGER1.batt_minus_1

custom parts:
  Neopixel Ring 16: Neopixel Ring x16
  MAX4466 Electret Microphone Breakout Board: MAX4466 Electrec Microphone Breakout Board
