# Fritzing sketch bb_soundEffect_module (saved by Fritzing 0.9.2b)
breadboards: 1

parts:
  Part1 = Spark Core (v1.0)
  C1 = Electrolytic Capacitor [capacitance=1000μF package="1010 [SMD, electrolytic]"]
  U1 = LIPO-2000mAh [package=lipo-2000]
  CHARGER1 = USB_LiIon_LiPoly_Charger_v1.2
  Q1 = NPN-Transistor [part_number=S9013 package="TO92 [THT]"]
  R1 = Resistor [tolerance=±5% resistance=470 package="1206 [SMD]"]
  SP1 = SPEAKER [package=pcb_mount_speaker]

nets:
  N1: Part1.GND, C1.-, CHARGER1.load_minus_1, Q1.C
  N2: Part1.VIN, C1.+, CHARGER1.load_plus_1, SP1.-
  N3: Part1.D0, Part1.D6
  N4: U1.+, CHARGER1.batt_plus_1
  N5: U1.-, CHARGER1.batt_minus_1
  N6: Q1.E, SP1.+
  N7: Q1.B, R1.Pin_0
