# Fritzing sketch breadboard_fritzing (saved by Fritzing 0.9.2b)
breadboards: 1

parts:
  SG1 = Buzzer 12mm [package=buzzer-12mm-ns]
  R1 = Resistor [tolerance=±5% resistance=330 package="0603 [SMD]"]
  Part1 = Arduino Uno (Rev3) - ICSP
  U1 = POT [package=pot_alpha_rv16af-20]
  R4 = Resistor [tolerance=±5% resistance=10k package="0603 [SMD]"]
  R3 = Resistor [tolerance=±5% resistance=270 package="0603 [SMD]"]
  R2 = Resistor [tolerance=±5% resistance=270 package="0603 [SMD]"]
  S1 = Momentary Switch [package=ksa_sealed_tac_switch]
  LED1 = LED - 5mm [color="Green (565nm)" package="5 mm [THT]"]
  LED2 = LED - 5mm [color="Red (633nm)" package="5 mm [THT]"]
  J1 = Basic Servo
  BAT1 = BC9VPC [package=bc9vpc]

nets:
  N1: SG1.1, R1.Pin_0
  N2: SG1.2, Part1.D8
  GND: R1.Pin_1, Part1.GND, S1.4, LED1.cathode, LED2.cathode, J1.gnd, BAT1.V-
  N3: Part1.A5/SCL, U1.S
  N4: Part1.D3_PWM, J1.pulse
  N5: Part1.D4, R3.Pin_1
  N6: Part1.D5_PWM, R2.Pin_1
  N7: Part1.D6_PWM, R4.Pin_0, S1.2
  5V: Part1.5V, U1.E, R4.Pin_1, J1.vcc
  N8: Part1.VIN, BAT1.V+
  N9: R3.Pin_0, LED2.anode
  N10: R2.Pin_0, LED1.anode
