# Fritzing sketch Neopixel-ATtiny (saved by Fritzing 0.9.2b)
breadboards: 1

parts:
  C1 = Electrolytic Capacitor [capacitance=330µF package="0807 [SMD, electrolytic]"]
  U3 = attiny85 [package=dip]
  Part1 = ws2812b [package="smd 2812b"]
  J1 = Power Jack [package=power_jack_pth_lock]
  IC2 = Voltage Regulator [package=78xxl]

nets:
  GND: C1.-, U3.Pin_4, Part1.VSS, J1.GND, IC2.GND
  N1: C1.+, U3.Pin_8, Part1.VDD, IC2.OUT
  N2: U3.Pin_2, Part1.DIN
  N3: J1.PWR, IC2.IN
