# Fritzing sketch RF-Sensor-ATtiny (saved by Fritzing 0.9.2b)
breadboards: 2

parts:
  U1 = RF-LINK_TX [package=rf-link_tx]
  U2 = RF-LINK_RX [package=rf-link_rx]
  Part1 = Arduino Uno (Rev3) - ICSP
  C1 = Electrolytic Capacitor [capacitance=330µF package="0807 [SMD, electrolytic]"]
  Q1 = PHOTOTRANSISTOR REFLECTIVE OBJECT SENSOR [package=qrb1114-side]
  R1 = Resistor [tolerance=±5% resistance=100 package="2010 [SMD]"]
  R2 = Resistor [tolerance=±5% resistance=10k package="2010 [SMD]"]
  U3 = attiny85 [package=dip]
  4xAAA_6V = Battery Holders [package=battery-aaa]
  R3 = Resistor [tolerance=±5% resistance=100 package="2010 [SMD]"]
  LED1 = LED - 3mm [color="Red (633nm)" package="3 mm [THT]"]

nets:
  N1: U1.GND, Q1.E, Q1.K, U3.Pin_4, 4xAAA_6V.-, LED1.cathode
  N2: U1.+5V, R1.Pin_1, R2.Pin_1, 4xAAA_6V.+
  GND: U2.GND, Part1.GND, C1.-
  N3: U2.DATA, Part1.D4
  +5V: U2.+5V, Part1.5V, C1.+
  N4: Q1.A, R1.Pin_0
  N5: Q1.C, R2.Pin_0, U3.Pin_2
  N6: U3.Pin_3, R3.Pin_1
  N7: R3.Pin_0, LED1.anode
