# Fritzing sketch RF-Sensor-Neopixel-ATtiny-rev (saved by Fritzing 0.9.2b)
breadboards: 2

parts:
  U1 = RF-LINK_TX [package=rf-link_tx]
  U2 = RF-LINK_RX [package=rf-link_rx]
  C1 = Electrolytic Capacitor [capacitance=330µF package="0807 [SMD, electrolytic]"]  # not connected
  Q1 = PHOTOTRANSISTOR REFLECTIVE OBJECT SENSOR [package=qrb1114-side]
  R1 = Resistor [tolerance=±5% resistance=100 package="2010 [SMD]"]
  R2 = Resistor [tolerance=±5% resistance=10k package="2010 [SMD]"]
  4xAAA_6V = Battery Holders [package=battery-aaa]
  R3 = Resistor [tolerance=±5% resistance=100 package="2010 [SMD]"]
  LED1 = LED - 3mm [color="Red (633nm)" package="3 mm [THT]"]
  U4 = attiny85 [package=dip]
  Part2 = ws2812b [package="smd 2812b"]
  J2 = Power Jack [package=power_jack_pth_lock]
  IC3 = Voltage Regulator [package=78xxl]
  U3 = attiny85 [package=dip]
  D1 = Diode [package=diode-1n4001]
  Q2 = TRANSISTOR_NPN [package=to-92]

nets (from the breadboard view):
  N1: U1.GND, 4xAAA_6V.-, LED1.cathode, U3.Pin_4, Q2.C
  N2: U1.+5V, R1.Pin_1, R2.Pin_1, 4xAAA_6V.+
  GND: U2.GND, U4.Pin_4, J2.GND, IC3.GND
  N3: U2.DATA, U4.Pin_6
  +5V: U2.+5V, U4.Pin_8, Part2.VDD, IC3.OUT, D1.A
  N4: Q1.A, R1.Pin_0
  N5: Q1.C, R2.Pin_0, U3.Pin_2
  N6: Q1.E, Q1.K, Q2.E
  N7: R3.Pin_0, LED1.anode
  N8: R3.Pin_1, U3.Pin_3
  N9: U4.Pin_2, Part2.DIN
  N10: Part2.VSS, D1.C
  N11: J2.PWR, IC3.IN
