# Fritzing sketch RF-sensor-test (saved by Fritzing 0.9.2b)
breadboards: 2

parts:
  U1 = RF-LINK_TX [package=rf-link_tx]
  U2 = RF-LINK_RX [package=rf-link_rx]
  Part1 = Arduino Uno (Rev3) - ICSP
  Part2 = Arduino Uno (Rev3) - ICSP
  C1 = Electrolytic Capacitor [capacitance=330µF package="0807 [SMD, electrolytic]"]
  Q1 = PHOTOTRANSISTOR REFLECTIVE OBJECT SENSOR [package=qrb1114-side]
  R1 = Resistor [tolerance=±5% resistance=100 package="2010 [SMD]"]
  R2 = Resistor [tolerance=±5% resistance=10k package="2010 [SMD]"]

nets:
  N1: U1.DATA, Part2.D4
  GND: U1.GND, Part2.GND, Q1.E, Q1.K
  +5V: U1.+5V, Part2.5V, R1.Pin_1, R2.Pin_1
  GND_2: U2.GND, Part1.GND, C1.-
  N2: U2.DATA, Part1.D4
  +5V_2: U2.+5V, Part1.5V, C1.+
  N3: Part2.A0, Q1.C, R2.Pin_0
  N4: Q1.A, R1.Pin_0
