# Fritzing sketch RF-transmission-test (saved by Fritzing 0.9.2b)
breadboards: 2

parts:
  U1 = RF-LINK_TX [package=rf-link_tx]
  U2 = RF-LINK_RX [package=rf-link_rx]
  Part1 = Arduino Uno (Rev3) - ICSP
  Part2 = Arduino Uno (Rev3) - ICSP
  C1 = Electrolytic Capacitor [capacitance=330µF package="0807 [SMD, electrolytic]"]

nets:
  N1: U1.DATA, Part2.D4
  GND: U1.GND, Part2.GND
  +5V: U1.+5V, Part2.5V
  GND_2: U2.GND, Part1.GND, C1.-
  N2: U2.DATA, Part1.D4
  +5V_2: U2.+5V, Part1.5V, C1.+
