# Fritzing sketch bb_complete_circuit (saved by Fritzing 0.9.2b)
breadboards: 1

parts:
  C1 = Electrolytic Capacitor [capacitance=1000μF package="1010 [SMD, electrolytic]"]
  U1 = LIPO-2000mAh [package=lipo-2000]
  CHARGER1 = USB_LiIon_LiPoly_Charger_v1.2
  neopixel1 = Neopixel Ring 16
  MIC1 = MAX4466 Electret Microphone Breakout Board
  D1 = Diode [package=diode-1n4148]
  Q1 = NPN-Transistor [package="TO92 [THT]"]
  R2 = Resistor [tolerance=±5% resistance=470 package="1206 [SMD]"]
  R3 = Resistor [tolerance=±5% resistance=470 package="1206 [SMD]"]
  Part2 = HC-SR04 Ultrasonic Rangemeter
  J1 = Basic Servo
  Part1 = Spark Core (v1.0)
  SP1 = SPEAKER [package=pcb_mount_speaker]
  R1 = Resistor [tolerance=±5% resistance=470 package="1206 [SMD]"]

nets:
  VCC: C1.-, CHARGER1.load_plus_1, neopixel1.VCC, D1.C, Part2.VCC, J1.vcc, Part1.VIN, SP1.-
  GND: C1.+, CHARGER1.load_minus_1, neopixel1.GND, MIC1.GND, D1.A, Q1.C, Part2.GND, J1.gnd, Part1.GND, R1.Pin_1
  N1: U1.+, CHARGER1.batt_plus_1
  N2: U1.-, CHARGER1.batt_minus_1
  N3: neopixel1.IN, Part1.D2
  N4: MIC1.out, Part1.A0
  N5: MIC1.VCC, Part1.3V3*
  N6: Q1.E, SP1.+
  N7: Q1.B, R3.Pin_0
  N8: R2.Pin_0, Part1.D5, R1.Pin_0
  N9: R2.Pin_1, Part2.Echo
  N10: R3.Pin_1, Part1.D6
  N11: Part2.Trig, Part1.D4
  N12: J1.pulse, Part1.D1

custom parts:
  Neopixel Ring 16: Neopixel Ring x16
  MAX4466 Electret Microphone Breakout Board: MAX4466 Electrec Microphone Breakout Board
